# Fritzing sketch Arduino-Temp-Hum-Logger (saved by Fritzing 0.9.2b)
breadboards: 1

parts:
  RTC1 = Real Time Clock Module - DS1307 RTC Breakout Board
  U2 = RF-LINK_TX [package=rf-link_tx]
  ANT1 = Antenna
  Part1 = Arduino Uno (Rev3)
  RHT1 = Humidity and Temperature Sensor RHT03
  C1 = Ceramic Capacitor [capacitance=100nF package="0603 [SMD, multilayer]"]
  R1 = Resistor [tolerance=±5% resistance=220 package="0805 [SMD]"]

nets:
  5V: RTC1.5V, U2.+5V, Part1.5V, RHT1.Vcc, C1.1, R1.Pin_0
  GND: RTC1.GND, U2.GND, Part1.GND, RHT1.GND_2, C1.0
  N1: RTC1.SCL, Part1.A5/SCL
  N2: RTC1.SDA, Part1.A4/SDA
  N3: U2.ANT, ANT1.antenna_lead
  N4: U2.DATA, Part1.D12/MISO
  N5: Part1.D2, RHT1.Data-signal, R1.Pin_1
